// Logisim project exo1.circ as structural Verilog: 1 circuit, main circuit main
module main (
  input  a,
  input  b,
  output out_3,
  output a_b,
  output a_b_2
);

  wire and_3_out, and_4_out, not_1_out, not_2_out, undriven;

  not not_1 (not_1_out, a);
  not not_2 (not_2_out, b);
  and and_1 (out_3, a, not_2_out);
  and and_2 (a_b, not_1_out, b);
  and and_3 (and_3_out, a, b, undriven);
  and and_4 (and_4_out, undriven, not_2_out, not_1_out);
  or or_1 (a_b_2, and_3_out, and_4_out);

  // Notes on the sheet:
  //   a>b
endmodule
