// Logisim project exo2.circ as structural Verilog: 4 circuits, main circuit main
module main (
  input  [3:0] in_1,
  input  [3:0] in_2,
  output out_3,
  output out_4,
  output out_5,
  output out_6,
  output out_7
);

  add_4bit add_4bit_1 (.a(in_1), .b(in_2), .c0(out_3), .c1(out_4), .c2(out_5), .c3(out_6), .R(out_7));
endmodule

module add_demi_bit (
  input  x,
  input  y,
  output S,
  output R
);

  xor xor_1 (S, x, y);
  and and_1 (R, x, y);
endmodule

module add_1bit (
  input  a,
  input  b,
  input  R0,
  output S,
  output R1
);

  wire add_demi_bit_1_r, add_demi_bit_1_s, add_demi_bit_2_r;

  add_demi_bit add_demi_bit_1 (.x(a), .y(b), .S(add_demi_bit_1_s), .R(add_demi_bit_1_r));
  add_demi_bit add_demi_bit_2 (.x(R0), .y(add_demi_bit_1_s), .S(S), .R(add_demi_bit_2_r));
  or or_1 (R1, add_demi_bit_2_r, add_demi_bit_1_r);

  // Notes on the sheet:
  //   add 1/2bit
  //   add 1/2bit
endmodule

module add_4bit (
  input  [3:0] a,
  input  [3:0] b,
  output c0,
  output c1,
  output c2,
  output c3,
  output R
);

  wire add_1bit_1_r1, add_1bit_2_r1, add_1bit_3_r1, and_1_out, not_1_out;

  not not_1 (not_1_out, a[0]);
  and and_1 (and_1_out, not_1_out, a[0]);
  add_1bit add_1bit_1 (.a(b[0]), .b(a[0]), .R0(and_1_out), .S(c0), .R1(add_1bit_1_r1));
  add_1bit add_1bit_2 (.a(b[1]), .b(a[1]), .R0(add_1bit_1_r1), .S(c1), .R1(add_1bit_2_r1));
  add_1bit add_1bit_3 (.a(b[2]), .b(a[2]), .R0(add_1bit_2_r1), .S(c2), .R1(add_1bit_3_r1));
  add_1bit add_1bit_4 (.a(b[3]), .b(a[3]), .R0(add_1bit_3_r1), .S(c3), .R1(R));
endmodule
