// Logisim project projet.circ as structural Verilog: 3 circuits, main circuit main
module main (
  input  [7:0] Input,
  input  \E__1_activé_0_desac ,
  input  \Code_opé_0_dépiler_1_empiler ,
  input  [7:0] in_4,
  input  Clear,
  input  [7:0] Input_2,
  output [7:0] out_7,
  output \Débordement ,
  output [7:0] Output,
  output [7:0] out_10,
  output [7:0] out_11,
  output Debordement,
  output [7:0] Output_2
);

  wire and_1_out, and_3_out, clock_1_out, comparator_1_eq, comparator_1_gt, comparator_1_lt, comparator_2_eq,
       comparator_2_lt, nor_1_out, nor_2_out, not_1_out, or_1_out, or_2_out, or_3_out, xor_1_out;
  wire [1:0] counter_1_q, multiplexer_2_out;
  wire [7:0] controlled_buffer_1_out, multiplexer_1_out, Pile_2_output, register_1_q, Unit_calcul_2_s;

  Pile Pile (
    .Input(Input), .E(\E__1_activé_0_desac ), .\Code_opé (\Code_opé_0_dépiler_1_empiler ), .Clear(Clear),
    .Output(out_7));
  Comparator comparator_1 (
    .a(Input_2), .b({8{1'b0}}), .gt(comparator_1_gt), .eq(comparator_1_eq), .lt(comparator_1_lt));
  and and_1 (and_1_out, comparator_1_lt, Input_2[7]);
  Comparator comparator_2 (.a(out_7), .b({8{1'b0}}), .eq(comparator_2_eq), .lt(comparator_2_lt));  // open: gt
  or or_1 (or_1_out, comparator_1_gt, comparator_1_lt, comparator_1_eq);
  or or_2 (or_2_out, Input_2[0], Input_2[1]);
  nor nor_1 (nor_1_out, Input_2[0], Input_2[1]);
  nor nor_2 (nor_2_out, Input_2[2], Input_2[3], Input_2[4], Input_2[5], Input_2[6]);
  // AND_Gate and_2 has open pins: in0=out_7[7], in1=comparator_2_lt, out=open
  Multiplexer #(.width(8), .enable("false")) multiplexer_1 (
    .in0(Input_2), .in1(Unit_calcul_2_s), .out(multiplexer_1_out), .sel(counter_1_q[1]));
  Pile Pile_2 (.Input(multiplexer_1_out), .E(or_1_out), .\Code_opé (xor_1_out), .Output(Pile_2_output));  // open: Clear
  xor xor_1 (xor_1_out, comparator_1_lt, not_1_out);
  not not_1 (not_1_out, comparator_1_eq);
  or or_3 (or_3_out, or_2_out, nor_1_out);
  Demultiplexer #(.select(2), .width(8), .enable("false")) demultiplexer_1 (
    .out0(out_10), .out1(out_11), .in(controlled_buffer_1_out), .sel(counter_1_q));  // open: out2, out3
  assign controlled_buffer_1_out = not_1_out ? Pile_2_output : 8'bz;  // Controlled_Buffer controlled_buffer_1
  Clock clock_1 (.out(clock_1_out));
  and and_3 (and_3_out, or_3_out, and_1_out, nor_2_out);
  Counter #(.width(2), .max('h3)) counter_1 (.Q(counter_1_q), .clk(clock_1_out));  // open: load, D, count, carry, clr
  Multiplexer #(.width(2)) multiplexer_2 (
    .in1(Input_2[1:0]), .out(multiplexer_2_out), .sel(and_3_out), .en(and_3_out));  // open: in0
  Register register_1 (.D(out_10), .en(counter_1_q[1]), .Q(register_1_q), .clk(clock_1_out));  // open: clr
  \Unité_de_calcul  Unit_calcul ();  // open: A, B, Code_opé, D, S
  Multiplexer #(.width(8), .enable("false")) multiplexer_3 (
    .in1(Pile_2_output), .out({Debordement, Output_2[6:0]}), .sel(comparator_1_eq));  // open: in0
  Multiplexer #(.width(8), .enable("false")) multiplexer_4 (
    .in0(out_7), .in1(in_4), .out(Output), .sel(comparator_2_eq));
  \Unité_de_calcul  Unit_calcul_2 (
    .A(register_1_q), .B(out_11), .\Code_opé (multiplexer_2_out), .S(Unit_calcul_2_s));  // open: D

  assign Output_2[7] = Debordement;

  // Notes on the sheet:
  //   > numero 127| = fin | < op
  //   > numero 127| = fin | < op
  //   1=code op/00 fin/numero sinon 0-127
  //   code op
  //   ssi bit pf 1 et code op valide
endmodule

module \Unité_de_calcul  (
  input  [7:0] A,
  input  [7:0] B,
  input  [1:0] \Code_opé ,
  output D,
  output [7:0] S
);

  wire adder_1_cout, comparator_1_eq, comparator_2_eq, not_1_out;
  wire [3:0] multiplier_2_out;
  wire [7:0] adder_1_out, divider_1_out, multiplier_1_out, subtractor_1_out;

  Adder adder_1 (.a(A), .b(B), .out(adder_1_out), .cout(adder_1_cout));  // open: cin
  Subtractor subtractor_1 (.a(A), .b(B), .out(subtractor_1_out));  // open: bin, bout
  Multiplier multiplier_1 (.a(A), .b(B), .out(multiplier_1_out));  // open: cin, cout
  Divider divider_1 (.a(A), .b(B), .out(divider_1_out));  // open: upper, rem
  Multiplier #(.width(4)) multiplier_2 (.a(A[7:4]), .b(B[7:4]), .out(multiplier_2_out));  // open: cin, cout
  Comparator comparator_1 (.a(B), .b({8{1'b0}}), .eq(comparator_1_eq));  // open: gt, lt
  Comparator #(.width(4)) comparator_2 (.a(multiplier_2_out), .b(4'b0000), .eq(comparator_2_eq));  // open: gt, lt
  not not_1 (not_1_out, comparator_2_eq);
  Multiplexer #(.select(2), .width(8)) multiplexer_1 (
    .in0(adder_1_out), .in1(subtractor_1_out), .in2(multiplier_1_out), .in3(divider_1_out), .out(S),
    .sel(\Code_opé ), .en(1'b1));
  Multiplexer #(.select(2)) multiplexer_2 (
    .in0(adder_1_cout), .in1(1'b0), .in2(not_1_out), .in3(comparator_1_eq), .out(D), .sel(\Code_opé ),
    .en(1'b1));

  // Notes on the sheet:
  //   Overflow impossible
  //   with 2 unsigned int
  //   Result *
  //   Overflow *
  //   Result +
  //   Overflow +
  //   Result /
  //   Overflow /
  //   Result -
  //   S : sortie du calcul
  //   A, B : Paramètres du calcul
  //   D : Indication si le résultat a débordé
  //   Code opé : Code d'opération (00+, 01-, 10*, 11/)
endmodule

module Pile (
  input  [7:0] Input,
  input  E,
  input  \Code_opé ,
  input  Clear,
  output [7:0] Output
);

  wire and_1_out, CLK_out, counter_1_carry, not_1_out, not_2_out, not_3_out;
  wire [7:0] counter_1_q;

  not not_1 (not_1_out, \Code_opé );
  Counter counter_1 (
    .load(not_1_out), .count(1'b1), .Q(counter_1_q), .carry(counter_1_carry), .clk(CLK_out), .clr(Clear));  // open: D
  not not_2 (not_2_out, counter_1_carry);
  Clock CLK (.out(CLK_out));
  and and_1 (and_1_out, not_2_out, E);
  not not_3 (not_3_out, \Code_opé );
  RAM #(.bus("separate")) ram_1 (
    .addr(counter_1_q), .din(Input), .data(Output), .str(\Code_opé ), .sel(and_1_out), .clk(CLK_out),
    .ld(not_3_out), .clr(Clear));

  // Notes on the sheet:
  //   E : si E = 0, la pile conserve le contenu, sinon elle réalise une opération
  //   Input : Entrée de données
  //   Output : Sortie de données
  //   Code opé : 0 dépiler, 1 empiler
endmodule
